// Logisim project DigitLock.circ as structural Verilog: 1 circuit, main circuit main
module main (
  input  C,
  input  clk
);

  wire and_1_out, and_2_out, and_3_out, and_4_out, and_5_out, and_6_out, and_7_out, and_8_out, and_9_out,
       and_10_out, and_11_out, and_12_out, and_14_out, and_15_out, D0_q, D0_qn, D1_q, D1_qn, D2_q, D2_qn,
       D3_q, D3_qn, D4_q, D4_qn, D5_qn, D6_qn, D7_qn, not_1_out, or_1_out, or_2_out, or_3_out, or_4_out,
       or_5_out, undriven;

  and and_1 (and_1_out, C, D2_q);
  and and_2 (and_2_out, C, and_15_out);
  and and_3 (and_3_out, C, and_9_out);
  and and_4 (and_4_out, C, and_6_out);
  or or_1 (or_1_out, and_7_out, and_11_out);
  or or_2 (or_2_out, and_11_out, and_3_out);
  or or_3 (or_3_out, and_1_out, and_5_out, and_4_out);
  or or_4 (or_4_out, and_2_out, and_14_out, and_5_out);
  or or_5 (or_5_out, and_14_out, and_5_out);
  and and_5 (and_5_out, and_8_out, C);
  D_Flip_Flop D0 (.D(C), .clk(clk), .Q(D0_q), .Qn(D0_qn), .reset(undriven));  // open: preset
  D_Flip_Flop D1 (.D(or_1_out), .clk(clk), .Q(D1_q), .Qn(D1_qn), .preset(undriven));  // open: reset
  D_Flip_Flop D2 (.D(or_2_out), .clk(clk), .Q(D2_q), .Qn(D2_qn));  // open: preset, reset
  D_Flip_Flop D3 (.D(or_3_out), .clk(clk), .Q(D3_q), .Qn(D3_qn));  // open: preset, reset
  D_Flip_Flop D4 (.D(or_4_out), .clk(clk), .Q(D4_q), .Qn(D4_qn));  // open: preset, reset
  D_Flip_Flop D5 (.D(or_5_out), .clk(clk), .Qn(D5_qn));  // open: Q, preset, reset
  D_Flip_Flop D6 (.D(and_5_out), .clk(clk), .Qn(D6_qn));  // open: Q, preset, reset
  D_Flip_Flop D7 (.D(and_5_out), .clk(clk), .Qn(D7_qn));  // open: Q, preset, reset
  and and_6 (and_6_out, D0_qn, D1_qn, D3_q, D4_qn, D5_qn, D6_qn, D7_qn);
  and and_7 (and_7_out, C, D0_q);
  and and_8 (and_8_out, D0_q, D1_q);
  and and_9 (and_9_out, D1_q, D2_q);
  and and_10 (and_10_out, D5_qn, D6_qn, D7_qn);
  and and_11 (and_11_out, and_8_out, D2_qn);
  not not_1 (not_1_out, D2_qn);
  and and_12 (and_12_out, D3_q, D4_q);
  // AND_Gate and_13 has open pins: in0=D3_qn, in1=D4_q, out=open
  and and_14 (and_14_out, and_8_out, D2_qn, and_12_out, and_10_out);
  and and_15 (and_15_out, and_7_out, not_1_out, and_10_out);
endmodule
